# Fritzing sketch device (saved by Fritzing 0.6.4b)
breadboards: 1

parts:
  K2 = LH1500AT_Solid_State_Relay_DIP_6
  K1 = LH1500AT_Solid_State_Relay_DIP_6
  TS5 = Maxim___Dallas_18B20_Temperature_Sensor [part_number="DS18B20\r"]
  TS4 = Maxim___Dallas_18B20_Temperature_Sensor [part_number="DS18B20\r"]
  TS3 = Maxim___Dallas_18B20_Temperature_Sensor [part_number="DS18B20\r"]
  TS2 = Maxim___Dallas_18B20_Temperature_Sensor [part_number="DS18B20\r"]
  TS1 = Maxim___Dallas_18B20_Temperature_Sensor [part_number="DS18B20\r"]
  U1 = Voltage Regulator - 5V [package="TO220 [THT]"]
  PP1 = Power plug
  WP1 = DC Motor
  R1 = Resistor [tolerance=±5% resistance=220 package="1206 [SMD]"]
  QSP1 = P8X32A_QuickStart [part_number=40000]
  U2 = Voltage Regulator - 5V [package="TO220 [THT]"]
  U3 = Voltage Regulator - 5V [package="TO220 [THT]"]
  U4 = Voltage Regulator - 5V [package="TO220 [THT]"]
  C1 = Ceramic Capacitor [capacitance=10µF voltage=20V package="100 mil [THT, multilayer]"]
  R2 = Resistor [tolerance=±5% resistance=4.7k package=THT]
  R3 = Resistor [tolerance=±5% resistance=4.7k package=THT]
  R4 = Resistor [tolerance=±5% resistance=4.7k package=THT]
  R5 = Resistor [tolerance=±5% resistance=4.7k package=THT]
  R6 = Resistor [tolerance=±5% resistance=4.7k package=THT]

nets:
  N1: K2.connector0, QSP1.connector14
  GND: K2.connector1, K1.connector1, TS5.connector3, TS4.connector3, TS3.connector3, TS2.connector3, TS1.connector3, U1.GND, PP1.GND, WP1.pin_1, R1.Pin_0, QSP1.connector18, U2.GND, U3.GND, U4.GND, C1.1
  N2: K2.connector3, WP1.pin_2
  N3: K2.connector5, U1.output_voltage, QSP1.connector19, U2.output_voltage, U3.output_voltage, U4.output_voltage
  N4: K1.connector0, QSP1.connector13
  N5: K1.connector3, R1.Pin_1
  N6: K1.connector5, U1.input_voltage, PP1.VCC, U2.input_voltage, U3.input_voltage, U4.input_voltage, C1.0
  N7: TS5.connector4, QSP1.connector12, R6.Pin_0
  N8: TS5.connector5, TS4.connector5, TS3.connector5, TS2.connector5, TS1.connector5, QSP1.connector17, R2.Pin_1, R3.Pin_1, R4.Pin_1, R5.Pin_1, R6.Pin_1
  N9: TS4.connector4, QSP1.connector11, R5.Pin_0
  N10: TS3.connector4, QSP1.connector10, R4.Pin_0
  N11: TS2.connector4, QSP1.connector9, R3.Pin_0
  N12: TS1.connector4, QSP1.connector8, R2.Pin_0
